# Fritzing sketch Project (saved by Fritzing 0.9.4)
circuit board: 8.46667cm x 5.64444cm
breadboards: 1

parts:
  HC-SR04_Sensor_1 = HC-SR04 Ultrasonic Distance Sensor
  Part5 = Arduino Uno (Rev3) - ICSP  # not connected
  VCC1 = 4 x AAA Battery Mount
  Mod2 = Arduino Sensor Shield v5.0
  M5 = Dagu DGServo 9g (Top view) [part_number=RS001B]
  S2 = H-Bridge with L298N
  M6 = DC Motor
  M7 = DC Motor
  R5 = Resistor [tolerance=±5% resistance=220 package=THT]
  R6 = Resistor [tolerance=±5% resistance=220 package="0805 [SMD]"]
  LED7 = LED - 3mm [color="White (4500K)" package="3 mm [THT]"]
  LED8 = LED - 3mm [color="White (4500K)" package="3 mm [THT]"]
  Part6 = KY-022 Infrared Receiver Module [package="Breakout board"]

nets:
  VCC: HC-SR04_Sensor_1.VCC, Mod2.13-V, Mod2.11-V, Mod2.8-V, Mod2.3-V, Mod2.ParallelLCD-VCC, M5.vcc, Part6.Vin
  N1: HC-SR04_Sensor_1.TRIG, Mod2.9-S, Mod2.ParallelLCD-D9
  N2: HC-SR04_Sensor_1.ECHO, Mod2.8-S, Mod2.ParallelLCD-D8
  GND: HC-SR04_Sensor_1.GND, Mod2.A0-GND, Mod2.11-G, Mod2.8-G, Mod2.3-G, Mod2.SerialLCD-GND, M5.gnd, R5.Pin_1, R6.Pin_1, Part6.-
  N3: VCC1.-, S2.GND
  N4: VCC1.+, S2.12V
  N5: Mod2.URF01-A0, Mod2.A0-SIG, LED7.anode
  N6: Mod2.URF01-A1, Mod2.A1-SIG, LED8.anode
  N7: Mod2.12-S, Mod2.ParallelLCD-D12, S2.IN4
  N8: Mod2.11-S, Part6.S
  N9: Mod2.7-S, Mod2.ParallelLCD-D7, S2.IN3
  N10: Mod2.6-S, Mod2.ParallelLCD-D6, S2.ENB
  N11: Mod2.5-S, Mod2.ParallelLCD-D5, S2.ENA
  N12: Mod2.4-S, Mod2.SerialLCD-D4, S2.IN2
  N13: Mod2.3-S, Mod2.ParallelLCD-D3, M5.pulse
  N14: Mod2.2-S, Mod2.SerialLCD-D2, S2.IN1
  N15: S2.M1-01, M6.pin_2
  N16: S2.M1-02, M6.pin_1
  N17: S2.M2-01, M7.pin_2
  N18: S2.M2-02, M7.pin_1
  N19: R5.Pin_0, LED8.cathode
  N20: R6.Pin_0, LED7.cathode

notes:
  Battery also connects to this port to the right

custom parts:
  Arduino Sensor Shield v5.0: Arduino Sensor Shield v5.0 provides I2C interface, Bluetooth module communication interface, SD card module communication interface, APC220 wireless RF modules communication interface, RB URF V1.1 ultrasonic sensors interface, 12864 LCD serial and parallel interface, 32 servo controller interfaces. In addition (with the sel jumper removed) allows an external power supply for the servos as the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
  H-Bridge with L298N: h-bridge
  KY-022 Infrared Receiver Module: Arduino IR receiver module KY-022, reacts to 38kHz infrared light.

// code stored in the sketch: Start.ino
/*--------------------------------------------------------------------
Name:   Brandon Ramos
Date:   9/28/2020
Course: CSCE 236 Embedded Systems (Fall 2020) 
HW/Lab: Lab 3


Purp: Start of Robot


Doc:  Datasheets and course website, powerpoints and TA help


Academic Integrity Statement: I certify that, while others may have 
assisted me in brain storming, debugging and validating this program, 
the program itself is my own work. I understand that submitting code 
which is the work of other individuals is a violation of the honor   
code.  I also understand that if I knowingly give my original work to 
another individual is also a violation of the honor code.
--------------------------------------------------------------------*/


#include <Arduino.h>
#include <avr/io.h>


// Definitions for Port B & D registors
#define PINB_Reg (*((volatile uint8_t *) 0x23)) //Reads the state of INPUT pin
#define DDRB_Reg (*((volatile uint8_t *) 0x24)) // I/O register, if set high the state is an output
#define PORTB_Reg (*((volatile uint8_t *) 0x25)) //Determines if pin is HIGH or LOW


#define PIND_Reg (*((volatile uint8_t *) 0x29)) //Reads the state of INPUT pin
#define DDRD_Reg (*((volatile uint8_t *) 0x2a)) // I/O register, if set high the state is an output
#define PORTD_Reg (*((volatile uint8_t *) 0x2b)) //Determines if pin is HIGH or LOW


// Definitions for LED assignments:
#define BOARD_LED 5   //pin 13 is PortB bit 5
#define LeftLED 7     //pin 7 is PortD bit 7
#define RightLED 4    //pin 12 is PortB bit 4
#define SERVO 3     //pin 9 is PORTD bit 1
#define trigPin 1 //pin 9 is PortB bit 1
#define echoPin 0 // pin 8 is PortB bit 0


void setup() {                
  Serial.begin(9600);
  Serial.println("Starting up...");


  DDRD_Reg |= (1<<SERVO); //sets pin 3 to output
  DDRB_Reg |= (1<<trigPin); //set pin 9 to output
  DDRB_Reg &= ~(1<<echoPin); //set pin 8 to input
  DDRB_Reg |=  (1<<RightLED); //set pin 12 to output
  DDRD_Reg |= (1<<LeftLED);   //set pin 7 to output


  //Init counter2 for Servo
  TCCR2A = 0;
  TCCR2A |= (1<< COM2A1) | (1<<COM2B1) | (1<<WGM20); //the inversion for phase correct
  TCCR2B |= (1<<CS22) | (1<<CS21) | (1<<CS20); //Clock T1 with prescalar of 1024
  OCR2A = 156; //top
  OCR2B = 10; //input capture
  //Make sure interrupts are disabled 
  TIMSK2 = 0;
  TIFR2 = 0;
  
  //Init counter 1 for Ultrasonic Sensor
  TCCR1A = 0; //0xffff top, rolls over
  TCCR1B = (1<<CS11);//8 prescaler
  TCCR1C = 0;
  //set counter to zero, high byte first
  TCNT1H = 0;
  TCNT1L = 0;
  //make sure inerrupts are disabled
  TIMSK1 = 0;
  TIFR1 = 0;


  Serial.println("Finished setup!");
}


void servoLeft(){
  // Serial.println("Servo Looks Left");  
  OCR2B = 18; //value so servo turns left
}
void servoStraight(){
  // Serial.println("Servo Looks Ahead");
  OCR2B = 10; //value so servo straightens out
}
void servoRight(){
  // Serial.println("Servo Looks Right");
  OCR2B = 3; //value so servo turns right
}


int sonicSensor(){
  int distance; //value that is returned
  unsigned long echo; //will hold the #cycles it took for pulse 
  double distanceInInches; //conversion


  // Clears the trigPin
  PORTB_Reg &= ~(1<<trigPin);
  delayMicroseconds(2);
  // Sets the trigPin on HIGH state for 10 micro seconds
  PORTB_Reg |= (1<<trigPin);
  delayMicroseconds(10);
  PORTB_Reg &= ~(1<<trigPin);
  TCNT1 = 0;//resets timer to 0
  // delay(1);
  echo = ICR1; //ICR1 will be 
  // Serial.println(ICR1);


  //echo*(8/2)*340m/s*39.37in/m 
  //8 is prescaler, 2 is half the distance
  distanceInInches = (echo*4*340*39.37);
  distanceInInches = distanceInInches/16000000;
  distanceInInches -= 3;
  distance = distanceInInches;
  // Serial.print("Object is: ");
  if(distance < 0){ distance=0;}
  Serial.print(distance);
  Serial.println(" Inches away!");


  return distance; //return value in inches
}


void checkoff3(){
  // int  race = sonicSensor();
  // servoLeft();
  // delay(2000);
  // if(sonicSensor()<=12){
  //   //turn on left led for 2 seconds
  //   PORTD_Reg |= (1<<LeftLED);
  //   delay(2000);
  //   PORTD_Reg &= ~(1<<LeftLED);
  // }
  servoRight();
  delay(2000);
  if(sonicSensor()<=12){
    //turn on right led for 2 seconds
    PORTB_Reg |= (1<<RightLED);
    delay(2000);
    PORTB_Reg &= ~(1<<RightLED);
  }
  servoStraight();
  delay(2000);
  if(sonicSensor()<=12){
    //turn on both leds for 2 seconds
    PORTB_Reg |= (1<<RightLED);
    PORTD_Reg |= (1<<LeftLED);
    delay(2000);
    PORTB_Reg &= ~(1<<RightLED);
    PORTD_Reg &= ~(1<<LeftLED);
  }
}


// //data for graph
// void checkoff3_5(){
//   servoStraight();
//   delay(500);
//   int temp = sonicSensor();
//   delay(3000);
//    temp = sonicSensor();
//   delay(3000);
//    temp = sonicSensor();
//   delay(3000);
// }


void loop() {
// servoLeft();
// delay(1000);
// servoRight();
// delay(1000);
// servoStraight();
// delay(1000);
// sonicSensor();
checkoff3();
}


/**
 * Ultrasonic Sensor Boards
 * 1.) 340meters/second
 * 2.)t=(2in)(2.54/1in)(1m/100cm)/(340m/s)=149.4us
 * 3.)Range(2cm->4m) and apparently has a 3mm accuracy
 * 4.)Minimum measurement cycle is 60ms where the working frequency is 25ms
 * 
 * 5.)If it takes longern than 8/340=23ms to come back then dont use the info
 * 6.)
 * 7.)
 * 8.)No, it will need a delay since the code is ran long after it still moves
 * 9.)send many and stop
 * 10.)
 **/
